// Logisim project Labs.circ as structural Verilog: 7 circuits, main circuit 4_reg
module _4_reg (
  input  INPR,
  input  DR,
  input  AC,
  input  AND,
  input  Cin,
  input  ADD,
  input  COMP,
  input  LD_DR,
  input  LD_INPR,
  input  CIR,
  input  CIL,
  input  \AC_İ_1 ,
  input  \AC_İ_1_2 ,
  output Cout,
  output out_15
);

  wire ADD_out, adder_1_out, AND_out, COMP_out, ID_NPR_out, ID_OR_out, not_1_out, SHL_out, SHR_out;

  Adder #(.width(1)) adder_1 (.a(DR), .b(AC), .out(adder_1_out), .cin(Cin), .cout(Cout));
  not not_1 (not_1_out, AC);
  and u_AND (AND_out, AND, AC, DR);
  and u_ADD (ADD_out, ADD, adder_1_out);
  and u_COMP (COMP_out, COMP, not_1_out);
  and ID_OR (ID_OR_out, LD_DR, DR);
  and ID_NPR (ID_NPR_out, LD_INPR, INPR);
  and SHR (SHR_out, CIR, \AC_İ_1_2 );
  and SHL (SHL_out, CIL, \AC_İ_1 );
  or or_1 (out_15, AND_out, ADD_out, COMP_out, ID_OR_out, ID_NPR_out, SHR_out, SHL_out);
endmodule

module \_4_BİT_REG__LAB3  (
  input  INC,
  input  LD,
  input  [3:0] INPUT,
  input  CLR,
  input  clk,
  output [3:0] out_6
);

  wire and_1_out, and_2_out, and_3_out, and_4_out, and_5_out, and_6_out, and_7_out, and_8_out, and_9_out,
       and_10_out, and_11_out, and_12_out, not_1_out, not_2_out, not_3_out, not_4_out, not_5_out, not_6_out,
       or_1_out, or_2_out, or_3_out, or_4_out, or_5_out, or_6_out, or_7_out, or_8_out;

  not not_1 (not_1_out, LD);
  and and_1 (and_1_out, INC, not_1_out);
  not not_2 (not_2_out, not_1_out);
  not not_3 (not_3_out, INPUT[0]);
  not not_4 (not_4_out, INPUT[1]);
  not not_5 (not_5_out, INPUT[2]);
  not not_6 (not_6_out, INPUT[3]);
  and and_2 (and_2_out, not_2_out, INPUT[0]);
  and and_3 (and_3_out, not_2_out, not_3_out);
  buf and_4 (and_4_out, INPUT[1]);  // AND_Gate
  and and_5 (and_5_out, not_2_out, not_4_out);
  and and_6 (and_6_out, not_2_out, INPUT[2]);
  buf and_7 (and_7_out, not_5_out);  // AND_Gate
  and and_8 (and_8_out, not_2_out, INPUT[3]);
  and and_9 (and_9_out, not_2_out, not_6_out);
  or or_1 (or_1_out, and_2_out, and_1_out);
  or or_2 (or_2_out, and_3_out, and_1_out);
  or or_3 (or_3_out, and_4_out, and_10_out);
  and and_10 (and_10_out, and_1_out, out_6[0]);
  or or_4 (or_4_out, and_10_out, and_5_out);
  or or_5 (or_5_out, and_6_out, and_11_out);
  and and_11 (and_11_out, and_1_out, out_6[0], out_6[1]);
  or or_6 (or_6_out, and_11_out, and_7_out);
  or or_7 (or_7_out, and_8_out, and_12_out);
  and and_12 (and_12_out, and_1_out, out_6[0], out_6[1], out_6[2]);
  or or_8 (or_8_out, and_12_out, and_9_out);
  J_K_Flip_Flop j_k_ff_1 (.J(or_1_out), .clk(clk), .K(or_2_out), .Q(out_6[0]), .reset(CLR));  // open: Qn, preset, en
  J_K_Flip_Flop j_k_ff_2 (.J(or_3_out), .clk(clk), .K(or_4_out), .Q(out_6[1]), .reset(CLR));  // open: Qn, preset, en
  J_K_Flip_Flop j_k_ff_3 (.J(or_5_out), .clk(clk), .K(or_6_out), .Q(out_6[2]), .reset(CLR));  // open: Qn, preset, en
  J_K_Flip_Flop j_k_ff_4 (.J(or_7_out), .clk(clk), .K(or_8_out), .Q(out_6[3]), .reset(CLR));  // open: Qn, preset, en
endmodule

module _1_BIT_ALU__LAB5 (
  input  INPR,
  input  DR,
  input  AC,
  input  AND,
  input  Cin,
  input  ADD,
  input  COMP,
  input  LD_DR,
  input  LD_INPR,
  input  CIR,
  input  CIL,
  input  \AC_İ_1 ,
  input  \AC_İ_1_2 ,
  output Cout,
  output out_15
);

  wire ADD_out, adder_1_out, AND_out, COMP_out, ID_NPR_out, ID_OR_out, not_1_out, SHL_out, SHR_out;

  Adder #(.width(1)) adder_1 (.a(DR), .b(AC), .out(adder_1_out), .cin(Cin), .cout(Cout));
  not not_1 (not_1_out, AC);
  and u_AND (AND_out, AND, AC, DR);
  and u_ADD (ADD_out, ADD, adder_1_out);
  and u_COMP (COMP_out, COMP, not_1_out);
  and ID_OR (ID_OR_out, LD_DR, DR);
  and ID_NPR (ID_NPR_out, LD_INPR, INPR);
  and SHR (SHR_out, CIR, \AC_İ_1_2 );
  and SHL (SHL_out, CIL, \AC_İ_1 );
  or or_1 (out_15, AND_out, ADD_out, COMP_out, ID_OR_out, ID_NPR_out, SHR_out, SHL_out);
endmodule

module _4_BIT_ALU__LAB5 (
  input  Cin,
  input  [3:0] AC,
  input  E_AC_0,
  input  [3:0] DR,
  input  [3:0] INPR,
  input  AND,
  input  ADD,
  input  CMA,
  input  LD_DR,
  input  LD_INPR,
  input  CIR,
  input  CIL,
  input  in_13,
  output [3:0] out_14,
  output out_15
);

  wire n4_reg_1_cout, n4_reg_2_cout, n4_reg_3_cout;

  _4_reg u_4_reg_1 (
    .AND(AND), .ADD(ADD), .COMP(CMA), .LD_DR(LD_DR), .LD_INPR(LD_INPR), .CIR(CIR), .CIL(CIL),
    .\AC_İ_1 (E_AC_0), .\AC_İ_1_2 (AC[1]), .INPR(INPR[0]), .DR(DR[0]), .AC(AC[0]), .Cin(Cin),
    .Cout(n4_reg_1_cout), .out_15(out_14[0]));
  _4_reg u_4_reg_2 (
    .AND(AND), .ADD(ADD), .COMP(CMA), .LD_DR(LD_DR), .LD_INPR(LD_INPR), .CIR(CIR), .CIL(CIL),
    .\AC_İ_1 (AC[0]), .\AC_İ_1_2 (AC[2]), .INPR(INPR[1]), .DR(DR[1]), .AC(AC[1]), .Cin(n4_reg_1_cout),
    .Cout(n4_reg_2_cout), .out_15(out_14[1]));
  _4_reg u_4_reg_3 (
    .AND(AND), .ADD(ADD), .COMP(CMA), .LD_DR(LD_DR), .LD_INPR(LD_INPR), .CIR(CIR), .CIL(CIL),
    .\AC_İ_1 (AC[1]), .\AC_İ_1_2 (AC[3]), .INPR(INPR[2]), .DR(DR[2]), .AC(AC[2]), .Cin(n4_reg_2_cout),
    .Cout(n4_reg_3_cout), .out_15(out_14[2]));
  _4_reg u_4_reg_4 (
    .AND(AND), .ADD(ADD), .COMP(CMA), .LD_DR(LD_DR), .LD_INPR(LD_INPR), .CIR(CIR), .CIL(CIL),
    .\AC_İ_1 (AC[2]), .\AC_İ_1_2 (in_13), .INPR(INPR[3]), .DR(DR[3]), .AC(AC[3]), .Cin(n4_reg_3_cout),
    .Cout(out_15), .out_15(out_14[3]));
  \_4_BİT_REG__LAB3  \u_4_bi̇t_reg_lab3_1  ();  // open: INPUT, clk, LD, INC, CLR, out_6
endmodule

module LAB6 (
  input  T0,
  input  T1,
  input  T3,
  input  T4,
  input  D4,
  input  D5,
  input  D6,
  output PC_LD,
  output PC_INC,
  output PC_BUS
);

  wire and_1_out, and_2_out, and_3_out, or_1_out;

  or or_1 (or_1_out, D6, D4);
  and and_1 (and_1_out, or_1_out, T3);
  and and_2 (and_2_out, D5, T4);
  and and_3 (and_3_out, D5, T3);
  or or_2 (PC_LD, and_1_out, and_2_out);
  or or_3 (PC_BUS, and_3_out, T0);

  assign PC_INC = T1;
endmodule

module LAB1 (
  output A,
  output F1,
  output B,
  output C,
  output A_2,
  output F2,
  output B_2,
  output C_2
);

  wire and_1_out, and_2_out, and_3_out, and_4_out, and_5_out, and_6_out, nand_1_out, nand_2_out, not_1_out,
       not_2_out, or_1_out, or_2_out, undriven, undriven_2, undriven_3, undriven_4, undriven_5, undriven_6,
       xor_2_out;

  not not_1 (not_1_out, undriven);
  nand nand_1 (nand_1_out, undriven_2, undriven);
  not not_2 (not_2_out, undriven_3);
  or or_1 (or_1_out, nand_1_out, undriven_6);
  not nand_2 (nand_2_out, undriven_4);  // NAND_Gate
  buf or_2 (or_2_out, nand_2_out);  // OR_Gate
  and and_1 (and_1_out, nand_2_out, undriven_4);
  and and_2 (and_2_out, undriven_5, undriven_4);
  and and_3 (and_3_out, not_1_out, undriven_6);
  and and_4 (and_4_out, not_1_out, or_1_out);
  and and_5 (and_5_out, not_2_out, undriven_5);
  and and_6 (and_6_out, not_2_out, or_2_out);
  xor xor_1 (F1, and_3_out, and_4_out);
  xor xor_2 (xor_2_out, and_1_out, and_2_out);
  or or_3 (F2, and_5_out, and_6_out, xor_2_out);
endmodule

module LAB2 (
  input  Q1,
  input  Q0,
  input  _1,
  input  _1_2,
  input  Q3,
  input  Q2,
  input  Q1_2,
  input  Q0_2
);

  wire j_k_ff_2_q, undriven;

  J_K_Flip_Flop j_k_ff_1 (.J(j_k_ff_2_q), .clk(undriven), .Q(Q1));  // open: K, Qn, preset, en, reset
  J_K_Flip_Flop j_k_ff_2 (.J(_1), .clk(j_k_ff_2_q), .K(_1), .Q(j_k_ff_2_q));  // open: Qn, preset, en, reset

  // Notes on the sheet:
  //   CLK
  //   2 bit sayacı
  //   4 bit sayacı
endmodule
