// Logisim project lab6.circ as structural Verilog: 1 circuit, main circuit main
module main (
  input  T0,
  input  T1,
  input  T3,
  input  T4,
  input  D4,
  input  D5,
  input  D6,
  output PC_LD,
  output PC_INC,
  output PC_BUS
);

  wire and_1_out, and_2_out, and_3_out, or_1_out;

  or or_1 (or_1_out, D6, D4);
  and and_1 (and_1_out, or_1_out, T3);
  and and_2 (and_2_out, D5, T4);
  or or_2 (PC_LD, and_1_out, and_2_out);
  and and_3 (and_3_out, D5, T3);
  or or_3 (PC_BUS, and_3_out, T0);

  assign PC_INC = T1;
endmodule
